// Logisim project test-circuit.circ as structural Verilog: 1 circuit, main circuit main
module main (
  input  in_1,
  input  in_2,
  input  in_3,
  input  in_4,
  input  in_5,
  input  in_6,
  input  in_7,
  input  in_8,
  input  in_9,
  input  in_10,
  input  in_11,
  input  in_12,
  input  in_13,
  input  in_14,
  input  in_15,
  input  in_16,
  input  in_17,
  input  in_18,
  input  in_19,
  input  in_20,
  input  in_21,
  input  in_22,
  input  in_23,
  input  in_24,
  input  in_25,
  input  in_26,
  input  in_27,
  input  in_28,
  input  in_29,
  input  in_30,
  input  in_31,
  input  in_32,
  input  in_33,
  input  in_34,
  input  in_35,
  input  in_36,
  input  in_37,
  input  in_38,
  input  in_39,
  input  in_40,
  input  in_41,
  input  in_42,
  input  in_43,
  input  in_44
);

  wire d;
  wire [1:0] truth_table_1_p2;
  wire [14:10] karnaugh_map_2_p3;

  // truth_table truth_table_1: pin names not known; wires that end beside it: 16'h75a3, truth_table_1_p2[0], truth_table_1_p2[1], 16'h75a3, in_17
  // karnaugh_map karnaugh_map_1: pin names not known
  // karnaugh_map karnaugh_map_2: pin names not known; wires that end beside it: {in_42, 2'b11, in_35, in_34, 2'b11, in_28, in_25, in_23, in_22, 2'b11, in_19, truth_table_1_p2}, 1'b1, karnaugh_map_2_p3[10], karnaugh_map_2_p3[13], karnaugh_map_2_p3[14]
  // karnaugh_map karnaugh_map_3: pin names not known; wires that end beside it: {in_43, karnaugh_map_2_p3[14:13], in_38, in_36, karnaugh_map_2_p3[10], 1'b1, in_32, in_30, in_27, in_24, 2'b11, in_20, 2'b11}, in_39
  // karnaugh_map karnaugh_map_4: pin names not known; wires that end beside it: d, in_18
  // karnaugh_map karnaugh_map_5: pin names not known; wires that end beside it: {in_44, 2'b11, in_40, in_37, 2'b11, in_33, in_31, in_29, in_26, 2'b11, in_21, 2'b11}, in_41

  // Other names for the same wires on the sheet: a = in_1; p = in_16
endmodule
